// Logisim project Proj2starter_2.circ as structural Verilog: 5 circuits, main circuit regfile
module CPUmain (
  input  [31:0] in_1
);

  wire control_1_imm_sel, regfile_1_p2;
  wire [3:0] control_1_alu_code;
  wire [4:0] regfile_1_p3, regfile_1_p4, regfile_1_p5;
  wire [31:0] control_1_imm, multiplexer_1_out, regfile_1_p1, regfile_1_p6, regfile_1_p7;

  // regfile regfile_1: pin names not known; wires that end beside it: regfile_1_p1, regfile_1_p2, regfile_1_p3, regfile_1_p4, regfile_1_p5, regfile_1_p6, regfile_1_p7
  Control control_1 (
    .Inst(in_1), .rs(regfile_1_p4), .rt(regfile_1_p5), .rd(regfile_1_p3), .imm(control_1_imm),
    .reg_write_e(regfile_1_p2), .imm_sel(control_1_imm_sel), .ALU_code(control_1_alu_code));
  Multiplexer #(.width(32)) multiplexer_1 (
    .in0(regfile_1_p7), .in1(control_1_imm), .out(multiplexer_1_out), .sel(control_1_imm_sel));
  Bit_Extender bit_extender_1 ();  // open: in, out
  ALU alu_1 (.OP2(multiplexer_1_out), .OP1(regfile_1_p6), .ALU_CODE(control_1_alu_code), .Res(regfile_1_p1));

  // Notes on the sheet:
  //   SHOULD AT LEAST WORK FOR ADD, ADDI AND MULT
  //   SET THIS TO 0 IF YOU DO NOT WANT TO OVERWRITE REGISTERS ... EX MULT -- HI AND LOW LIVE  IN THE ALU
  //   FOR MULT YOU DON'T WANT TO CHANGE ANY REGISTERS
  //   MULITPLEXER USED TO DETERMINE WHETHER IT IS I TYPE OR R TYPE
  //   BASICALLLY MAKE THIS = TO ZERO TO TAKE THE R TYPE 
  //   USE THIS TO EXTEND NON 32 BIT NUMBERS INTO SIGNED 32 BIT NUMBERS
  //   ALU DOES ALL OPERATIONS ON EVERY OP1 AND OP2 FROM THE REGISTERS -- HOWEVER YOU NEED TO SPECIFY WHICH ONE TO GET FROM THE ALU CODE
endmodule

module regfile (
  input  [31:0] rd_data,
  input  [4:0] rs,
  input  [4:0] rt,
  input  write_e,
  input  [4:0] rd,
  output [31:0] rs_data,
  output [31:0] rt_data
);

  wire clock_1_out, demultiplexer_1_out0, demultiplexer_1_out1, demultiplexer_1_out2, demultiplexer_1_out3,
       demultiplexer_1_out4, demultiplexer_1_out5, demultiplexer_1_out6, demultiplexer_1_out7,
       demultiplexer_1_out8, demultiplexer_1_out9, demultiplexer_1_out10, demultiplexer_1_out11,
       demultiplexer_1_out12, demultiplexer_1_out13, demultiplexer_1_out14, demultiplexer_1_out15,
       demultiplexer_1_out16, demultiplexer_1_out17, demultiplexer_1_out18, demultiplexer_1_out19,
       demultiplexer_1_out20, demultiplexer_1_out21, demultiplexer_1_out22, demultiplexer_1_out23,
       demultiplexer_1_out24, demultiplexer_1_out25, demultiplexer_1_out26, demultiplexer_1_out27,
       demultiplexer_1_out28, demultiplexer_1_out29, demultiplexer_1_out30, demultiplexer_1_out31;
  wire [31:0] Reg1_at_q, reg2_q, reg3_q, reg4_q, reg5_q, reg6_q, reg7_q, reg8_q, reg9_q, reg10_q, reg11_q,
       reg12_q, reg13_q, reg14_q, reg15_q, reg16_q, reg17_q, reg18_q, reg19_q, reg20_q, reg21_q, reg22_q,
       reg23_q, reg24_q, reg25_q, reg26_q, reg27_q, reg28_q, reg29_q, reg30_q, reg31_q, register_1_q;

  Demultiplexer #(.select(5)) demultiplexer_1 (
    .out0(demultiplexer_1_out0), .out1(demultiplexer_1_out1), .out2(demultiplexer_1_out2),
    .out3(demultiplexer_1_out3), .out4(demultiplexer_1_out4), .out5(demultiplexer_1_out5),
    .out6(demultiplexer_1_out6), .out7(demultiplexer_1_out7), .out8(demultiplexer_1_out8),
    .out9(demultiplexer_1_out9), .out10(demultiplexer_1_out10), .out11(demultiplexer_1_out11),
    .out12(demultiplexer_1_out12), .out13(demultiplexer_1_out13), .out14(demultiplexer_1_out14),
    .out15(demultiplexer_1_out15), .out16(demultiplexer_1_out16), .out17(demultiplexer_1_out17),
    .out18(demultiplexer_1_out18), .out19(demultiplexer_1_out19), .out20(demultiplexer_1_out20),
    .out21(demultiplexer_1_out21), .out22(demultiplexer_1_out22), .out23(demultiplexer_1_out23),
    .out24(demultiplexer_1_out24), .out25(demultiplexer_1_out25), .out26(demultiplexer_1_out26),
    .out27(demultiplexer_1_out27), .out28(demultiplexer_1_out28), .out29(demultiplexer_1_out29),
    .out30(demultiplexer_1_out30), .out31(demultiplexer_1_out31), .in(write_e), .sel(rd));
  Register #(.width(32)) Reg1_at (
    .D({32{1'b0}}), .en(demultiplexer_1_out0), .clk(clock_1_out), .Q(Reg1_at_q));  // open: clr
  Register #(.width(32)) register_1 (
    .D(rd_data), .en(demultiplexer_1_out1), .clk(clock_1_out), .Q(register_1_q));  // open: clr
  Register #(.width(32)) reg2 (.D(rd_data), .en(demultiplexer_1_out2), .clk(clock_1_out), .Q(reg2_q));  // open: clr
  Register #(.width(32)) reg3 (.D(rd_data), .en(demultiplexer_1_out3), .clk(clock_1_out), .Q(reg3_q));  // open: clr
  Register #(.width(32)) reg4 (.D(rd_data), .en(demultiplexer_1_out4), .clk(clock_1_out), .Q(reg4_q));  // open: clr
  Register #(.width(32)) reg5 (.D(rd_data), .en(demultiplexer_1_out5), .clk(clock_1_out), .Q(reg5_q));  // open: clr
  Register #(.width(32)) reg6 (.D(rd_data), .en(demultiplexer_1_out6), .clk(clock_1_out), .Q(reg6_q));  // open: clr
  Register #(.width(32)) reg7 (.D(rd_data), .en(demultiplexer_1_out7), .clk(clock_1_out), .Q(reg7_q));  // open: clr
  Register #(.width(32)) reg8 (.D(rd_data), .en(demultiplexer_1_out8), .clk(clock_1_out), .Q(reg8_q));  // open: clr
  Register #(.width(32)) reg9 (.D(rd_data), .en(demultiplexer_1_out9), .clk(clock_1_out), .Q(reg9_q));  // open: clr
  Register #(.width(32)) reg10 (.D(rd_data), .en(demultiplexer_1_out10), .clk(clock_1_out), .Q(reg10_q));  // open: clr
  Register #(.width(32)) reg11 (.D(rd_data), .en(demultiplexer_1_out11), .clk(clock_1_out), .Q(reg11_q));  // open: clr
  Register #(.width(32)) reg12 (.D(rd_data), .en(demultiplexer_1_out12), .clk(clock_1_out), .Q(reg12_q));  // open: clr
  Register #(.width(32)) reg13 (.D(rd_data), .en(demultiplexer_1_out13), .clk(clock_1_out), .Q(reg13_q));  // open: clr
  Clock clock_1 (.out(clock_1_out));
  Register #(.width(32)) reg14 (.D(rd_data), .en(demultiplexer_1_out14), .clk(clock_1_out), .Q(reg14_q));  // open: clr
  Register #(.width(32)) reg15 (.D(rd_data), .en(demultiplexer_1_out15), .clk(clock_1_out), .Q(reg15_q));  // open: clr
  Register #(.width(32)) reg16 (.D(rd_data), .en(demultiplexer_1_out16), .clk(clock_1_out), .Q(reg16_q));  // open: clr
  Register #(.width(32)) reg17 (.D(rd_data), .en(demultiplexer_1_out17), .clk(clock_1_out), .Q(reg17_q));  // open: clr
  Register #(.width(32)) reg18 (.D(rd_data), .en(demultiplexer_1_out18), .clk(clock_1_out), .Q(reg18_q));  // open: clr
  Register #(.width(32)) reg19 (.D(rd_data), .en(demultiplexer_1_out19), .clk(clock_1_out), .Q(reg19_q));  // open: clr
  Register #(.width(32)) reg20 (.D(rd_data), .en(demultiplexer_1_out20), .clk(clock_1_out), .Q(reg20_q));  // open: clr
  Register #(.width(32)) reg21 (.D(rd_data), .en(demultiplexer_1_out21), .clk(clock_1_out), .Q(reg21_q));  // open: clr
  Register #(.width(32)) reg22 (.D(rd_data), .en(demultiplexer_1_out22), .clk(clock_1_out), .Q(reg22_q));  // open: clr
  Register #(.width(32)) reg23 (.D(rd_data), .en(demultiplexer_1_out23), .clk(clock_1_out), .Q(reg23_q));  // open: clr
  Register #(.width(32)) reg24 (.D(rd_data), .en(demultiplexer_1_out24), .clk(clock_1_out), .Q(reg24_q));  // open: clr
  Register #(.width(32)) reg25 (.D(rd_data), .en(demultiplexer_1_out25), .clk(clock_1_out), .Q(reg25_q));  // open: clr
  Register #(.width(32)) reg26 (.D(rd_data), .en(demultiplexer_1_out26), .clk(clock_1_out), .Q(reg26_q));  // open: clr
  Register #(.width(32)) reg27 (.D(rd_data), .en(demultiplexer_1_out27), .clk(clock_1_out), .Q(reg27_q));  // open: clr
  Register #(.width(32)) reg28 (.D(rd_data), .en(demultiplexer_1_out28), .clk(clock_1_out), .Q(reg28_q));  // open: clr
  Register #(.width(32)) reg29 (.D(rd_data), .en(demultiplexer_1_out29), .clk(clock_1_out), .Q(reg29_q));  // open: clr
  Register #(.width(32)) reg30 (.D(rd_data), .en(demultiplexer_1_out30), .clk(clock_1_out), .Q(reg30_q));  // open: clr
  Register #(.width(32)) reg31 (.D(rd_data), .en(demultiplexer_1_out31), .clk(clock_1_out), .Q(reg31_q));  // open: clr
  Multiplexer #(.select(5), .width(32)) multiplexer_1 (
    .in0(Reg1_at_q), .in1(register_1_q), .in2(reg2_q), .in3(reg3_q), .in4(reg4_q), .in5(reg5_q),
    .in6(reg6_q), .in7(reg7_q), .in8(reg8_q), .in9(reg9_q), .in10(reg10_q), .in11(reg11_q), .in12(reg12_q),
    .in13(reg13_q), .in14(reg14_q), .in15(reg15_q), .in16(reg16_q), .in17(reg17_q), .in18(reg18_q),
    .in19(reg19_q), .in20(reg20_q), .in21(reg21_q), .in22(reg22_q), .in23(reg23_q), .in24(reg24_q),
    .in25(reg25_q), .in26(reg26_q), .in27(reg27_q), .in28(reg28_q), .in29(reg29_q), .in30(reg30_q),
    .in31(reg31_q), .out(rs_data), .sel(rs));
  Multiplexer #(.select(5), .width(32)) multiplexer_2 (
    .in0(Reg1_at_q), .in1(register_1_q), .in2(reg2_q), .in3(reg3_q), .in4(reg4_q), .in5(reg5_q),
    .in6(reg6_q), .in7(reg7_q), .in8(reg8_q), .in9(reg9_q), .in10(reg10_q), .in11(reg11_q), .in12(reg12_q),
    .in13(reg13_q), .in14(reg14_q), .in15(reg15_q), .in16(reg16_q), .in17(reg17_q), .in18(reg18_q),
    .in19(reg19_q), .in20(reg20_q), .in21(reg21_q), .in22(reg22_q), .in23(reg23_q), .in24(reg24_q),
    .in25(reg25_q), .in26(reg26_q), .in27(reg27_q), .in28(reg28_q), .in29(reg29_q), .in30(reg30_q),
    .in31(reg31_q), .out(rt_data), .sel(rt));

  // Notes on the sheet:
  //   reg1
  //   rs
endmodule

module ALU (
  input  [31:0] OP1,
  input  [31:0] OP2,
  input  [3:0] ALU_CODE,
  output [31:0] Res
);

  wire clock_1_out, comparator_1_gt, comparator_2_eq, comparator_3_eq, comparator_4_lt, comparator_5_lt,
       comparator_6_lt, comparator_7_lt, comparator_8_lt, comparator_9_lt, comparator_10_lt,
       comparator_11_lt, comparator_12_lt, comparator_13_lt, comparator_14_lt, comparator_15_lt,
       comparator_16_lt, comparator_17_lt, comparator_18_lt, comparator_19_lt, comparator_20_lt,
       comparator_21_lt, comparator_22_lt, comparator_23_lt, comparator_24_lt, comparator_25_lt,
       comparator_26_lt, comparator_27_lt, comparator_28_lt, comparator_29_lt, comparator_30_lt,
       comparator_31_lt, comparator_32_lt, comparator_33_lt, comparator_34_lt, comparator_35_lt,
       comparator_36_eq, comparator_36_gt, comparator_37_eq, comparator_37_gt, comparator_38_eq,
       comparator_38_gt, comparator_39_eq, comparator_39_gt, comparator_40_eq, comparator_40_gt,
       comparator_41_eq, comparator_41_gt, comparator_42_eq, comparator_42_gt, comparator_43_eq,
       comparator_43_gt, comparator_44_eq, comparator_44_gt, comparator_45_eq, comparator_45_gt,
       comparator_46_eq, comparator_46_gt, comparator_47_eq, comparator_47_gt, comparator_48_eq,
       comparator_48_gt, comparator_49_eq, comparator_49_gt, comparator_50_eq, comparator_50_gt,
       comparator_51_eq, comparator_51_gt, comparator_52_eq, comparator_52_gt, comparator_53_eq,
       comparator_53_gt, comparator_54_eq, comparator_54_gt, comparator_55_eq, comparator_55_gt,
       comparator_56_eq, comparator_56_gt, comparator_57_eq, comparator_57_gt, comparator_58_eq,
       comparator_58_gt, comparator_59_eq, comparator_59_gt, comparator_60_eq, comparator_60_gt,
       comparator_61_eq, comparator_61_gt, comparator_62_eq, comparator_62_gt, comparator_63_eq,
       comparator_63_gt, comparator_64_eq, comparator_64_gt, comparator_65_eq, comparator_65_gt,
       comparator_66_eq, comparator_66_gt, comparator_67_eq, comparator_67_gt, or_2_out, or_3_out, or_4_out,
       or_5_out, or_6_out, or_7_out, or_8_out, or_9_out, or_10_out, or_11_out, or_12_out, or_13_out,
       or_14_out, or_15_out, or_16_out, or_17_out, or_18_out, or_19_out, or_20_out, or_21_out, or_22_out,
       or_23_out, or_24_out, or_25_out, or_26_out, or_27_out, or_28_out, or_29_out, or_30_out, or_31_out,
       or_32_out, or_33_out, or_34_out;
  wire [4:0] bit_extender_1_out, bit_extender_3_out;
  wire [31:0] adder_1_out, adder_2_out, adder_3_out, adder_4_out, adder_5_out, adder_6_out, adder_7_out,
       adder_8_out, adder_9_out, adder_10_out, adder_11_out, adder_12_out, adder_13_out, adder_14_out,
       adder_15_out, adder_16_out, adder_17_out, adder_18_out, adder_19_out, adder_20_out, adder_21_out,
       adder_22_out, adder_23_out, adder_24_out, adder_25_out, adder_26_out, adder_27_out, adder_28_out,
       adder_29_out, adder_30_out, adder_31_out, adder_32_out, adder_33_out, adder_34_out, adder_35_out,
       adder_36_out, adder_37_out, adder_38_out, adder_39_out, adder_40_out, adder_41_out, adder_42_out,
       adder_43_out, adder_44_out, adder_45_out, adder_46_out, adder_47_out, adder_48_out, adder_49_out,
       adder_50_out, adder_51_out, adder_52_out, adder_53_out, adder_54_out, adder_55_out, adder_56_out,
       adder_57_out, adder_58_out, adder_59_out, adder_60_out, adder_61_out, adder_62_out, adder_63_out,
       and_1_out, bit_extender_2_out, bit_extender_4_out, bit_extender_5_out, bit_extender_6_out,
       bit_extender_7_out, bit_extender_8_out, bit_extender_9_out, bit_extender_10_out, bit_extender_11_out,
       bit_extender_12_out, bit_extender_13_out, bit_extender_14_out, bit_extender_15_out,
       bit_extender_16_out, bit_extender_17_out, bit_extender_18_out, bit_extender_19_out,
       bit_extender_20_out, bit_extender_21_out, bit_extender_22_out, bit_extender_23_out,
       bit_extender_24_out, bit_extender_25_out, bit_extender_26_out, bit_extender_27_out,
       bit_extender_28_out, bit_extender_29_out, bit_extender_30_out, bit_extender_31_out,
       bit_extender_32_out, bit_extender_33_out, bit_extender_34_out, bit_extender_35_out,
       bit_extender_37_out, bit_extender_38_out, bit_extender_39_out, bit_extender_40_out,
       bit_extender_41_out, bit_extender_42_out, bit_extender_43_out, bit_extender_44_out,
       bit_extender_45_out, bit_extender_46_out, bit_extender_47_out, bit_extender_48_out,
       bit_extender_49_out, bit_extender_50_out, bit_extender_51_out, bit_extender_52_out,
       bit_extender_53_out, bit_extender_54_out, bit_extender_55_out, bit_extender_56_out,
       bit_extender_57_out, bit_extender_58_out, bit_extender_59_out, bit_extender_60_out,
       bit_extender_61_out, bit_extender_62_out, bit_extender_63_out, bit_extender_64_out,
       bit_extender_65_out, bit_extender_66_out, bit_extender_67_out, bit_extender_68_out, divider_1_out,
       divider_1_rem, HI_q, LO_q, multiplexer_1_out, multiplexer_2_out, multiplier_1_cout, multiplier_1_out,
       nor_1_out, or_1_out, shifter_1_out, shifter_2_out, subtractor_1_out;
  wire [63:0] bit_extender_36_out;

  Bit_Extender #(.in_width(32), .out_width(5)) bit_extender_1 (.in(OP2), .out(bit_extender_1_out));
  assign and_1_out = OP2 & OP1;  // AND_Gate and_1, 32 bits wide
  Adder #(.width(32)) adder_1 (.a(OP1), .b(OP2), .out(adder_1_out));  // open: cin, cout
  Subtractor #(.width(32)) subtractor_1 (.a(OP1), .b(OP2), .out(subtractor_1_out));  // open: bin, bout
  Multiplier #(.width(32)) multiplier_1 (
    .a(OP1), .b(OP2), .out(multiplier_1_out), .cout(multiplier_1_cout));  // open: cin
  Divider #(.width(32)) divider_1 (.a(OP1), .b(OP2), .out(divider_1_out), .rem(divider_1_rem));  // open: upper
  Shifter #(.width(32)) shifter_1 (.in(OP1), .\dist (bit_extender_1_out), .out(shifter_1_out));
  Shifter #(.shift("lr"), .width(32)) shifter_2 (.in(OP1), .\dist (bit_extender_1_out), .out(shifter_2_out));
  Comparator #(.width(32)) comparator_1 (.a(OP1), .b(OP2), .gt(comparator_1_gt));  // open: eq, lt
  assign or_1_out = OP1 | OP2;  // OR_Gate or_1, 32 bits wide
  assign bit_extender_2_out = {{31{1'b0}}, comparator_1_gt};  // Bit_Extender bit_extender_2
  assign nor_1_out = ~(OP1 | OP2);  // NOR_Gate nor_1, 32 bits wide
  assign bit_extender_3_out = {{1{1'b0}}, ALU_CODE};  // Bit_Extender bit_extender_3
  Comparator #(.width(5)) comparator_2 (.a(5'b00010), .b(bit_extender_3_out), .eq(comparator_2_eq));  // open: gt, lt
  Comparator #(.width(5)) comparator_3 (.a(5'b00011), .b(bit_extender_3_out), .eq(comparator_3_eq));  // open: gt, lt
  Comparator #(.width(64)) comparator_4 (
    .a(bit_extender_36_out), .b(64'h80000000), .lt(comparator_4_lt));  // open: gt, eq
  Comparator #(.width(64)) comparator_5 (
    .a(bit_extender_36_out), .b(64'h40000000), .lt(comparator_5_lt));  // open: gt, eq
  Comparator #(.width(64)) comparator_6 (
    .a(bit_extender_36_out), .b(64'h20000000), .lt(comparator_6_lt));  // open: gt, eq
  Comparator #(.width(64)) comparator_7 (
    .a(bit_extender_36_out), .b(64'h10000000), .lt(comparator_7_lt));  // open: gt, eq
  Comparator #(.width(64)) comparator_8 (
    .a(bit_extender_36_out), .b(64'h8000000), .lt(comparator_8_lt));  // open: gt, eq
  Comparator #(.width(64)) comparator_9 (
    .a(bit_extender_36_out), .b(64'h4000000), .lt(comparator_9_lt));  // open: gt, eq
  Comparator #(.width(64)) comparator_10 (
    .a(bit_extender_36_out), .b(64'h2000000), .lt(comparator_10_lt));  // open: gt, eq
  Comparator #(.width(64)) comparator_11 (
    .a(bit_extender_36_out), .b(64'h1000000), .lt(comparator_11_lt));  // open: gt, eq
  Comparator #(.width(64)) comparator_12 (
    .a(bit_extender_36_out), .b(64'h800000), .lt(comparator_12_lt));  // open: gt, eq
  Comparator #(.width(64)) comparator_13 (
    .a(bit_extender_36_out), .b(64'h400000), .lt(comparator_13_lt));  // open: gt, eq
  Comparator #(.width(64)) comparator_14 (
    .a(bit_extender_36_out), .b(64'h200000), .lt(comparator_14_lt));  // open: gt, eq
  Comparator #(.width(64)) comparator_15 (
    .a(bit_extender_36_out), .b(64'h100000), .lt(comparator_15_lt));  // open: gt, eq
  Comparator #(.width(64)) comparator_16 (
    .a(bit_extender_36_out), .b(64'h80000), .lt(comparator_16_lt));  // open: gt, eq
  Comparator #(.width(64)) comparator_17 (
    .a(bit_extender_36_out), .b(64'h40000), .lt(comparator_17_lt));  // open: gt, eq
  Comparator #(.width(64)) comparator_18 (
    .a(bit_extender_36_out), .b(64'h20000), .lt(comparator_18_lt));  // open: gt, eq
  Comparator #(.width(64)) comparator_19 (
    .a(bit_extender_36_out), .b(64'h10000), .lt(comparator_19_lt));  // open: gt, eq
  Comparator #(.width(64)) comparator_20 (
    .a(bit_extender_36_out), .b(64'h8000), .lt(comparator_20_lt));  // open: gt, eq
  Comparator #(.width(64)) comparator_21 (
    .a(bit_extender_36_out), .b(64'h4000), .lt(comparator_21_lt));  // open: gt, eq
  Comparator #(.width(64)) comparator_22 (
    .a(bit_extender_36_out), .b(64'h2000), .lt(comparator_22_lt));  // open: gt, eq
  Comparator #(.width(64)) comparator_23 (
    .a(bit_extender_36_out), .b(64'h1000), .lt(comparator_23_lt));  // open: gt, eq
  Comparator #(.width(64)) comparator_24 (.a(bit_extender_36_out), .b(64'h800), .lt(comparator_24_lt));  // open: gt, eq
  Comparator #(.width(64)) comparator_25 (.a(bit_extender_36_out), .b(64'h400), .lt(comparator_25_lt));  // open: gt, eq
  Comparator #(.width(64)) comparator_26 (.a(bit_extender_36_out), .b(64'h200), .lt(comparator_26_lt));  // open: gt, eq
  Comparator #(.width(64)) comparator_27 (.a(bit_extender_36_out), .b(64'h100), .lt(comparator_27_lt));  // open: gt, eq
  Comparator #(.width(64)) comparator_28 (.a(bit_extender_36_out), .b(64'h80), .lt(comparator_28_lt));  // open: gt, eq
  Comparator #(.width(64)) comparator_29 (.a(bit_extender_36_out), .b(64'h40), .lt(comparator_29_lt));  // open: gt, eq
  Comparator #(.width(64)) comparator_30 (.a(bit_extender_36_out), .b(64'h20), .lt(comparator_30_lt));  // open: gt, eq
  Comparator #(.width(64)) comparator_31 (.a(bit_extender_36_out), .b(64'h10), .lt(comparator_31_lt));  // open: gt, eq
  Comparator #(.width(64)) comparator_32 (.a(bit_extender_36_out), .b(64'h8), .lt(comparator_32_lt));  // open: gt, eq
  Comparator #(.width(64)) comparator_33 (.a(bit_extender_36_out), .b(64'h4), .lt(comparator_33_lt));  // open: gt, eq
  Comparator #(.width(64)) comparator_34 (.a(bit_extender_36_out), .b(64'h2), .lt(comparator_34_lt));  // open: gt, eq
  Comparator #(.width(64)) comparator_35 (.a(bit_extender_36_out), .b(64'h1), .lt(comparator_35_lt));  // open: gt, eq
  assign bit_extender_4_out = {{31{1'b0}}, comparator_4_lt};  // Bit_Extender bit_extender_4
  assign bit_extender_5_out = {{31{1'b0}}, comparator_5_lt};  // Bit_Extender bit_extender_5
  assign bit_extender_6_out = {{31{1'b0}}, comparator_6_lt};  // Bit_Extender bit_extender_6
  assign bit_extender_7_out = {{31{1'b0}}, comparator_7_lt};  // Bit_Extender bit_extender_7
  assign bit_extender_8_out = {{31{1'b0}}, comparator_8_lt};  // Bit_Extender bit_extender_8
  assign bit_extender_9_out = {{31{1'b0}}, comparator_9_lt};  // Bit_Extender bit_extender_9
  assign bit_extender_10_out = {{31{1'b0}}, comparator_10_lt};  // Bit_Extender bit_extender_10
  assign bit_extender_11_out = {{31{1'b0}}, comparator_11_lt};  // Bit_Extender bit_extender_11
  assign bit_extender_12_out = {{31{1'b0}}, comparator_12_lt};  // Bit_Extender bit_extender_12
  assign bit_extender_13_out = {{31{1'b0}}, comparator_13_lt};  // Bit_Extender bit_extender_13
  assign bit_extender_14_out = {{31{1'b0}}, comparator_14_lt};  // Bit_Extender bit_extender_14
  assign bit_extender_15_out = {{31{1'b0}}, comparator_15_lt};  // Bit_Extender bit_extender_15
  assign bit_extender_16_out = {{31{1'b0}}, comparator_16_lt};  // Bit_Extender bit_extender_16
  assign bit_extender_17_out = {{31{1'b0}}, comparator_17_lt};  // Bit_Extender bit_extender_17
  assign bit_extender_18_out = {{31{1'b0}}, comparator_18_lt};  // Bit_Extender bit_extender_18
  assign bit_extender_19_out = {{31{1'b0}}, comparator_19_lt};  // Bit_Extender bit_extender_19
  assign bit_extender_20_out = {{31{1'b0}}, comparator_20_lt};  // Bit_Extender bit_extender_20
  assign bit_extender_21_out = {{31{1'b0}}, comparator_21_lt};  // Bit_Extender bit_extender_21
  assign bit_extender_22_out = {{31{1'b0}}, comparator_22_lt};  // Bit_Extender bit_extender_22
  assign bit_extender_23_out = {{31{1'b0}}, comparator_23_lt};  // Bit_Extender bit_extender_23
  assign bit_extender_24_out = {{31{1'b0}}, comparator_24_lt};  // Bit_Extender bit_extender_24
  assign bit_extender_25_out = {{31{1'b0}}, comparator_25_lt};  // Bit_Extender bit_extender_25
  assign bit_extender_26_out = {{31{1'b0}}, comparator_26_lt};  // Bit_Extender bit_extender_26
  assign bit_extender_27_out = {{31{1'b0}}, comparator_27_lt};  // Bit_Extender bit_extender_27
  assign bit_extender_28_out = {{31{1'b0}}, comparator_28_lt};  // Bit_Extender bit_extender_28
  assign bit_extender_29_out = {{31{1'b0}}, comparator_29_lt};  // Bit_Extender bit_extender_29
  assign bit_extender_30_out = {{31{1'b0}}, comparator_30_lt};  // Bit_Extender bit_extender_30
  assign bit_extender_31_out = {{31{1'b0}}, comparator_31_lt};  // Bit_Extender bit_extender_31
  assign bit_extender_32_out = {{31{1'b0}}, comparator_32_lt};  // Bit_Extender bit_extender_32
  assign bit_extender_33_out = {{31{1'b0}}, comparator_33_lt};  // Bit_Extender bit_extender_33
  assign bit_extender_34_out = {{31{1'b0}}, comparator_34_lt};  // Bit_Extender bit_extender_34
  assign bit_extender_35_out = {{31{1'b0}}, comparator_35_lt};  // Bit_Extender bit_extender_35
  Multiplexer #(.width(32)) multiplexer_1 (
    .in0(multiplier_1_cout), .in1(divider_1_out), .out(multiplexer_1_out), .sel(comparator_3_eq));
  Multiplexer #(.width(32)) multiplexer_2 (
    .in0(multiplier_1_out), .in1(divider_1_rem), .out(multiplexer_2_out), .sel(comparator_3_eq));
  Adder #(.width(32)) adder_2 (.a(bit_extender_6_out), .b(bit_extender_7_out), .out(adder_2_out));  // open: cin, cout
  Adder #(.width(32)) adder_3 (.a(bit_extender_10_out), .b(bit_extender_11_out), .out(adder_3_out));  // open: cin, cout
  Adder #(.width(32)) adder_4 (.a(bit_extender_12_out), .b(bit_extender_13_out), .out(adder_4_out));  // open: cin, cout
  Adder #(.width(32)) adder_5 (.a(bit_extender_16_out), .b(bit_extender_17_out), .out(adder_5_out));  // open: cin, cout
  Adder #(.width(32)) adder_6 (.a(bit_extender_20_out), .b(bit_extender_21_out), .out(adder_6_out));  // open: cin, cout
  Adder #(.width(32)) adder_7 (.a(bit_extender_22_out), .b(bit_extender_23_out), .out(adder_7_out));  // open: cin, cout
  Adder #(.width(32)) adder_8 (.a(bit_extender_26_out), .b(bit_extender_27_out), .out(adder_8_out));  // open: cin, cout
  Adder #(.width(32)) adder_9 (.a(bit_extender_30_out), .b(bit_extender_31_out), .out(adder_9_out));  // open: cin, cout
  Adder #(.width(32)) adder_10 (
    .a(bit_extender_32_out), .b(bit_extender_33_out), .out(adder_10_out));  // open: cin, cout
  Adder #(.width(32)) adder_11 (
    .a(bit_extender_34_out), .b(bit_extender_35_out), .out(adder_11_out));  // open: cin, cout
  or or_2 (or_2_out, comparator_2_eq, comparator_3_eq);
  Adder #(.width(32)) adder_12 (.a(bit_extender_4_out), .b(bit_extender_5_out), .out(adder_12_out));  // open: cin, cout
  Adder #(.width(32)) adder_13 (.a(bit_extender_8_out), .b(bit_extender_9_out), .out(adder_13_out));  // open: cin, cout
  Adder #(.width(32)) adder_14 (
    .a(bit_extender_14_out), .b(bit_extender_15_out), .out(adder_14_out));  // open: cin, cout
  Adder #(.width(32)) adder_15 (
    .a(bit_extender_18_out), .b(bit_extender_19_out), .out(adder_15_out));  // open: cin, cout
  Adder #(.width(32)) adder_16 (
    .a(bit_extender_24_out), .b(bit_extender_25_out), .out(adder_16_out));  // open: cin, cout
  Adder #(.width(32)) adder_17 (
    .a(bit_extender_28_out), .b(bit_extender_29_out), .out(adder_17_out));  // open: cin, cout
  Register #(.width(32)) HI (.D(multiplexer_1_out), .en(or_2_out), .clk(clock_1_out), .Q(HI_q));  // open: clr
  Register #(.width(32)) LO (.D(multiplexer_2_out), .en(or_2_out), .clk(clock_1_out), .Q(LO_q));  // open: clr
  Clock clock_1 (.out(clock_1_out));
  Adder #(.width(32)) adder_18 (.a(adder_12_out), .b(adder_19_out), .out(adder_18_out));  // open: cin, cout
  Adder #(.width(32)) adder_19 (.a(adder_2_out), .b(adder_13_out), .out(adder_19_out));  // open: cin, cout
  Adder #(.width(32)) adder_20 (.a(adder_3_out), .b(adder_4_out), .out(adder_20_out));  // open: cin, cout
  Adder #(.width(32)) adder_21 (.a(adder_14_out), .b(adder_22_out), .out(adder_21_out));  // open: cin, cout
  Adder #(.width(32)) adder_22 (.a(adder_5_out), .b(adder_15_out), .out(adder_22_out));  // open: cin, cout
  Adder #(.width(32)) adder_23 (.a(adder_6_out), .b(adder_7_out), .out(adder_23_out));  // open: cin, cout
  Adder #(.width(32)) adder_24 (.a(adder_16_out), .b(adder_25_out), .out(adder_24_out));  // open: cin, cout
  Adder #(.width(32)) adder_25 (.a(adder_8_out), .b(adder_17_out), .out(adder_25_out));  // open: cin, cout
  Adder #(.width(32)) adder_26 (.a(adder_9_out), .b(adder_10_out), .out(adder_26_out));  // open: cin, cout
  Adder #(.width(32)) adder_27 (.a(adder_18_out), .b(adder_20_out), .out(adder_27_out));  // open: cin, cout
  Adder #(.width(32)) adder_28 (.a(adder_21_out), .b(adder_23_out), .out(adder_28_out));  // open: cin, cout
  Adder #(.width(32)) adder_29 (.a(adder_24_out), .b(adder_26_out), .out(adder_29_out));  // open: cin, cout
  assign bit_extender_36_out = {{32{1'b0}}, OP1};  // Bit_Extender bit_extender_36
  Adder #(.width(32)) adder_30 (.a(adder_27_out), .b(adder_28_out), .out(adder_30_out));  // open: cin, cout
  Adder #(.width(32)) adder_31 (.a(adder_30_out), .b(adder_29_out), .out(adder_31_out));  // open: cin, cout
  Adder #(.width(32)) adder_32 (.a(adder_31_out), .b(adder_11_out), .out(adder_32_out));  // open: cin, cout
  Multiplexer #(.select(5), .width(32)) multiplexer_3 (
    .in0(adder_1_out), .in1(subtractor_1_out), .in2(multiplier_1_out), .in3(divider_1_out), .in4(HI_q),
    .in5(LO_q), .in6(shifter_1_out), .in7(shifter_2_out), .in8(bit_extender_2_out), .in9(and_1_out),
    .in10(or_1_out), .in11(nor_1_out), .in13(adder_32_out), .in14(adder_63_out), .out(Res),
    .sel(bit_extender_3_out));  // open: in12, in15, in16, in17, in18, in19, in20, in21, in22, in23, in24, in25, in26, in27, in28, in29, in30, in31
  Comparator #(.width(64)) comparator_36 (
    .a(bit_extender_36_out), .b(64'h80000000), .gt(comparator_36_gt), .eq(comparator_36_eq));  // open: lt
  Comparator #(.width(64)) comparator_37 (
    .a(bit_extender_36_out), .b(64'hc0000000), .gt(comparator_37_gt), .eq(comparator_37_eq));  // open: lt
  Comparator #(.width(64)) comparator_38 (
    .a(bit_extender_36_out), .b(64'he0000000), .gt(comparator_38_gt), .eq(comparator_38_eq));  // open: lt
  Comparator #(.width(64)) comparator_39 (
    .a(bit_extender_36_out), .b(64'hf0000000), .gt(comparator_39_gt), .eq(comparator_39_eq));  // open: lt
  Comparator #(.width(64)) comparator_40 (
    .a(bit_extender_36_out), .b(64'hf8000000), .gt(comparator_40_gt), .eq(comparator_40_eq));  // open: lt
  Comparator #(.width(64)) comparator_41 (
    .a(bit_extender_36_out), .b(64'hfc000000), .gt(comparator_41_gt), .eq(comparator_41_eq));  // open: lt
  Comparator #(.width(64)) comparator_42 (
    .a(bit_extender_36_out), .b(64'hfe000000), .gt(comparator_42_gt), .eq(comparator_42_eq));  // open: lt
  Comparator #(.width(64)) comparator_43 (
    .a(bit_extender_36_out), .b(64'hff000000), .gt(comparator_43_gt), .eq(comparator_43_eq));  // open: lt
  Comparator #(.width(64)) comparator_44 (
    .a(bit_extender_36_out), .b(64'hff800000), .gt(comparator_44_gt), .eq(comparator_44_eq));  // open: lt
  Comparator #(.width(64)) comparator_45 (
    .a(bit_extender_36_out), .b(64'hffc00000), .gt(comparator_45_gt), .eq(comparator_45_eq));  // open: lt
  Comparator #(.width(64)) comparator_46 (
    .a(bit_extender_36_out), .b(64'hffe00000), .gt(comparator_46_gt), .eq(comparator_46_eq));  // open: lt
  Comparator #(.width(64)) comparator_47 (
    .a(bit_extender_36_out), .b(64'hfff00000), .gt(comparator_47_gt), .eq(comparator_47_eq));  // open: lt
  Comparator #(.width(64)) comparator_48 (
    .a(bit_extender_36_out), .b(64'hfff80000), .gt(comparator_48_gt), .eq(comparator_48_eq));  // open: lt
  Comparator #(.width(64)) comparator_49 (
    .a(bit_extender_36_out), .b(64'hfffc0000), .gt(comparator_49_gt), .eq(comparator_49_eq));  // open: lt
  Comparator #(.width(64)) comparator_50 (
    .a(bit_extender_36_out), .b(64'hfffe0000), .gt(comparator_50_gt), .eq(comparator_50_eq));  // open: lt
  Comparator #(.width(64)) comparator_51 (
    .a(bit_extender_36_out), .b(64'hffff0000), .gt(comparator_51_gt), .eq(comparator_51_eq));  // open: lt
  Comparator #(.width(64)) comparator_52 (
    .a(bit_extender_36_out), .b(64'hffff8000), .gt(comparator_52_gt), .eq(comparator_52_eq));  // open: lt
  Comparator #(.width(64)) comparator_53 (
    .a(bit_extender_36_out), .b(64'hffffc000), .gt(comparator_53_gt), .eq(comparator_53_eq));  // open: lt
  Comparator #(.width(64)) comparator_54 (
    .a(bit_extender_36_out), .b(64'hffffe000), .gt(comparator_54_gt), .eq(comparator_54_eq));  // open: lt
  Comparator #(.width(64)) comparator_55 (
    .a(bit_extender_36_out), .b(64'hfffff000), .gt(comparator_55_gt), .eq(comparator_55_eq));  // open: lt
  Comparator #(.width(64)) comparator_56 (
    .a(bit_extender_36_out), .b(64'hfffff800), .gt(comparator_56_gt), .eq(comparator_56_eq));  // open: lt
  Comparator #(.width(64)) comparator_57 (
    .a(bit_extender_36_out), .b(64'hfffffc00), .gt(comparator_57_gt), .eq(comparator_57_eq));  // open: lt
  Comparator #(.width(64)) comparator_58 (
    .a(bit_extender_36_out), .b(64'hfffffe00), .gt(comparator_58_gt), .eq(comparator_58_eq));  // open: lt
  Comparator #(.width(64)) comparator_59 (
    .a(bit_extender_36_out), .b(64'hffffff00), .gt(comparator_59_gt), .eq(comparator_59_eq));  // open: lt
  Comparator #(.width(64)) comparator_60 (
    .a(bit_extender_36_out), .b(64'hffffff80), .gt(comparator_60_gt), .eq(comparator_60_eq));  // open: lt
  Comparator #(.width(64)) comparator_61 (
    .a(bit_extender_36_out), .b(64'hffffffc0), .gt(comparator_61_gt), .eq(comparator_61_eq));  // open: lt
  Comparator #(.width(64)) comparator_62 (
    .a(bit_extender_36_out), .b(64'hffffffe0), .gt(comparator_62_gt), .eq(comparator_62_eq));  // open: lt
  Comparator #(.width(64)) comparator_63 (
    .a(bit_extender_36_out), .b(64'hfffffff0), .gt(comparator_63_gt), .eq(comparator_63_eq));  // open: lt
  Comparator #(.width(64)) comparator_64 (
    .a(bit_extender_36_out), .b(64'hfffffff8), .gt(comparator_64_gt), .eq(comparator_64_eq));  // open: lt
  Comparator #(.width(64)) comparator_65 (
    .a(bit_extender_36_out), .b(64'hfffffffc), .gt(comparator_65_gt), .eq(comparator_65_eq));  // open: lt
  Comparator #(.width(64)) comparator_66 (
    .a(bit_extender_36_out), .b(64'hfffffffe), .gt(comparator_66_gt), .eq(comparator_66_eq));  // open: lt
  Comparator #(.width(64)) comparator_67 (
    .a(bit_extender_36_out), .b(64'hffffffff), .gt(comparator_67_gt), .eq(comparator_67_eq));  // open: lt
  or or_3 (or_3_out, comparator_36_gt, comparator_36_eq);
  or or_4 (or_4_out, comparator_37_gt, comparator_37_eq);
  or or_5 (or_5_out, comparator_38_gt, comparator_38_eq);
  assign bit_extender_37_out = {{31{1'b0}}, or_5_out};  // Bit_Extender bit_extender_37
  assign bit_extender_38_out = {{31{1'b0}}, or_6_out};  // Bit_Extender bit_extender_38
  or or_6 (or_6_out, comparator_39_gt, comparator_39_eq);
  or or_7 (or_7_out, comparator_40_gt, comparator_40_eq);
  or or_8 (or_8_out, comparator_41_gt, comparator_41_eq);
  or or_9 (or_9_out, comparator_42_gt, comparator_42_eq);
  or or_10 (or_10_out, comparator_43_gt, comparator_43_eq);
  or or_11 (or_11_out, comparator_44_gt, comparator_44_eq);
  or or_12 (or_12_out, comparator_45_gt, comparator_45_eq);
  or or_13 (or_13_out, comparator_46_gt, comparator_46_eq);
  or or_14 (or_14_out, comparator_47_gt, comparator_47_eq);
  assign bit_extender_39_out = {{31{1'b0}}, or_15_out};  // Bit_Extender bit_extender_39
  or or_15 (or_15_out, comparator_48_gt, comparator_48_eq);
  assign bit_extender_40_out = {{31{1'b0}}, or_16_out};  // Bit_Extender bit_extender_40
  or or_16 (or_16_out, comparator_49_gt, comparator_49_eq);
  or or_17 (or_17_out, comparator_50_gt, comparator_50_eq);
  or or_18 (or_18_out, comparator_51_gt, comparator_51_eq);
  or or_19 (or_19_out, comparator_52_gt, comparator_52_eq);
  or or_20 (or_20_out, comparator_53_gt, comparator_53_eq);
  or or_21 (or_21_out, comparator_54_gt, comparator_54_eq);
  or or_22 (or_22_out, comparator_55_gt, comparator_55_eq);
  or or_23 (or_23_out, comparator_56_gt, comparator_56_eq);
  or or_24 (or_24_out, comparator_57_gt, comparator_57_eq);
  assign bit_extender_41_out = {{31{1'b0}}, or_25_out};  // Bit_Extender bit_extender_41
  or or_25 (or_25_out, comparator_58_gt, comparator_58_eq);
  assign bit_extender_42_out = {{31{1'b0}}, or_26_out};  // Bit_Extender bit_extender_42
  or or_26 (or_26_out, comparator_59_gt, comparator_59_eq);
  or or_27 (or_27_out, comparator_60_gt, comparator_60_eq);
  or or_28 (or_28_out, comparator_61_gt, comparator_61_eq);
  or or_29 (or_29_out, comparator_62_gt, comparator_62_eq);
  or or_30 (or_30_out, comparator_63_gt, comparator_63_eq);
  or or_31 (or_31_out, comparator_64_gt, comparator_64_eq);
  or or_32 (or_32_out, comparator_65_gt, comparator_65_eq);
  or or_33 (or_33_out, comparator_66_gt, comparator_66_eq);
  or or_34 (or_34_out, comparator_67_gt, comparator_67_eq);
  assign bit_extender_43_out = {{31{1'b0}}, or_3_out};  // Bit_Extender bit_extender_43
  assign bit_extender_44_out = {{31{1'b0}}, or_4_out};  // Bit_Extender bit_extender_44
  Adder #(.width(32)) adder_33 (
    .a(bit_extender_37_out), .b(bit_extender_38_out), .out(adder_33_out));  // open: cin, cout
  assign bit_extender_45_out = {{31{1'b0}}, or_7_out};  // Bit_Extender bit_extender_45
  assign bit_extender_46_out = {{31{1'b0}}, or_8_out};  // Bit_Extender bit_extender_46
  assign bit_extender_47_out = {{31{1'b0}}, or_9_out};  // Bit_Extender bit_extender_47
  Adder #(.width(32)) adder_34 (
    .a(bit_extender_47_out), .b(bit_extender_48_out), .out(adder_34_out));  // open: cin, cout
  assign bit_extender_48_out = {{31{1'b0}}, or_10_out};  // Bit_Extender bit_extender_48
  assign bit_extender_49_out = {{31{1'b0}}, or_11_out};  // Bit_Extender bit_extender_49
  Adder #(.width(32)) adder_35 (
    .a(bit_extender_49_out), .b(bit_extender_50_out), .out(adder_35_out));  // open: cin, cout
  assign bit_extender_50_out = {{31{1'b0}}, or_12_out};  // Bit_Extender bit_extender_50
  assign bit_extender_51_out = {{31{1'b0}}, or_13_out};  // Bit_Extender bit_extender_51
  assign bit_extender_52_out = {{31{1'b0}}, or_14_out};  // Bit_Extender bit_extender_52
  Adder #(.width(32)) adder_36 (
    .a(bit_extender_39_out), .b(bit_extender_40_out), .out(adder_36_out));  // open: cin, cout
  assign bit_extender_53_out = {{31{1'b0}}, or_17_out};  // Bit_Extender bit_extender_53
  assign bit_extender_54_out = {{31{1'b0}}, or_18_out};  // Bit_Extender bit_extender_54
  assign bit_extender_55_out = {{31{1'b0}}, or_19_out};  // Bit_Extender bit_extender_55
  Adder #(.width(32)) adder_37 (
    .a(bit_extender_55_out), .b(bit_extender_56_out), .out(adder_37_out));  // open: cin, cout
  assign bit_extender_56_out = {{31{1'b0}}, or_20_out};  // Bit_Extender bit_extender_56
  assign bit_extender_57_out = {{31{1'b0}}, or_21_out};  // Bit_Extender bit_extender_57
  Adder #(.width(32)) adder_38 (
    .a(bit_extender_57_out), .b(bit_extender_58_out), .out(adder_38_out));  // open: cin, cout
  assign bit_extender_58_out = {{31{1'b0}}, or_22_out};  // Bit_Extender bit_extender_58
  assign bit_extender_59_out = {{31{1'b0}}, or_23_out};  // Bit_Extender bit_extender_59
  assign bit_extender_60_out = {{31{1'b0}}, or_24_out};  // Bit_Extender bit_extender_60
  Adder #(.width(32)) adder_39 (
    .a(bit_extender_41_out), .b(bit_extender_42_out), .out(adder_39_out));  // open: cin, cout
  assign bit_extender_61_out = {{31{1'b0}}, or_27_out};  // Bit_Extender bit_extender_61
  assign bit_extender_62_out = {{31{1'b0}}, or_28_out};  // Bit_Extender bit_extender_62
  assign bit_extender_63_out = {{31{1'b0}}, or_29_out};  // Bit_Extender bit_extender_63
  Adder #(.width(32)) adder_40 (
    .a(bit_extender_63_out), .b(bit_extender_64_out), .out(adder_40_out));  // open: cin, cout
  assign bit_extender_64_out = {{31{1'b0}}, or_30_out};  // Bit_Extender bit_extender_64
  assign bit_extender_65_out = {{31{1'b0}}, or_31_out};  // Bit_Extender bit_extender_65
  Adder #(.width(32)) adder_41 (
    .a(bit_extender_65_out), .b(bit_extender_66_out), .out(adder_41_out));  // open: cin, cout
  assign bit_extender_66_out = {{31{1'b0}}, or_32_out};  // Bit_Extender bit_extender_66
  assign bit_extender_67_out = {{31{1'b0}}, or_33_out};  // Bit_Extender bit_extender_67
  Adder #(.width(32)) adder_42 (
    .a(bit_extender_67_out), .b(bit_extender_68_out), .out(adder_42_out));  // open: cin, cout
  assign bit_extender_68_out = {{31{1'b0}}, or_34_out};  // Bit_Extender bit_extender_68
  Adder #(.width(32)) adder_43 (
    .a(bit_extender_43_out), .b(bit_extender_44_out), .out(adder_43_out));  // open: cin, cout
  Adder #(.width(32)) adder_44 (
    .a(bit_extender_45_out), .b(bit_extender_46_out), .out(adder_44_out));  // open: cin, cout
  Adder #(.width(32)) adder_45 (
    .a(bit_extender_51_out), .b(bit_extender_52_out), .out(adder_45_out));  // open: cin, cout
  Adder #(.width(32)) adder_46 (
    .a(bit_extender_53_out), .b(bit_extender_54_out), .out(adder_46_out));  // open: cin, cout
  Adder #(.width(32)) adder_47 (
    .a(bit_extender_59_out), .b(bit_extender_60_out), .out(adder_47_out));  // open: cin, cout
  Adder #(.width(32)) adder_48 (
    .a(bit_extender_61_out), .b(bit_extender_62_out), .out(adder_48_out));  // open: cin, cout
  Adder #(.width(32)) adder_49 (.a(adder_43_out), .b(adder_50_out), .out(adder_49_out));  // open: cin, cout
  Adder #(.width(32)) adder_50 (.a(adder_33_out), .b(adder_44_out), .out(adder_50_out));  // open: cin, cout
  Adder #(.width(32)) adder_51 (.a(adder_34_out), .b(adder_35_out), .out(adder_51_out));  // open: cin, cout
  Adder #(.width(32)) adder_52 (.a(adder_45_out), .b(adder_53_out), .out(adder_52_out));  // open: cin, cout
  Adder #(.width(32)) adder_53 (.a(adder_36_out), .b(adder_46_out), .out(adder_53_out));  // open: cin, cout
  Adder #(.width(32)) adder_54 (.a(adder_37_out), .b(adder_38_out), .out(adder_54_out));  // open: cin, cout
  Adder #(.width(32)) adder_55 (.a(adder_47_out), .b(adder_56_out), .out(adder_55_out));  // open: cin, cout
  Adder #(.width(32)) adder_56 (.a(adder_39_out), .b(adder_48_out), .out(adder_56_out));  // open: cin, cout
  Adder #(.width(32)) adder_57 (.a(adder_40_out), .b(adder_41_out), .out(adder_57_out));  // open: cin, cout
  Adder #(.width(32)) adder_58 (.a(adder_49_out), .b(adder_51_out), .out(adder_58_out));  // open: cin, cout
  Adder #(.width(32)) adder_59 (.a(adder_52_out), .b(adder_54_out), .out(adder_59_out));  // open: cin, cout
  Adder #(.width(32)) adder_60 (.a(adder_55_out), .b(adder_57_out), .out(adder_60_out));  // open: cin, cout
  Adder #(.width(32)) adder_61 (.a(adder_58_out), .b(adder_59_out), .out(adder_61_out));  // open: cin, cout
  Adder #(.width(32)) adder_62 (.a(adder_61_out), .b(adder_60_out), .out(adder_62_out));  // open: cin, cout
  Adder #(.width(32)) adder_63 (.a(adder_62_out), .b(adder_42_out), .out(adder_63_out));  // open: cin, cout

  // Notes on the sheet:
  //   I HAVE UPDATED THIS A LOT.... REVERT TO OTHER ONE FOR THE SETUP JUST FROM CLASS
  //   thinking about what we have to do.... if the ALU code is anything but mult or divide we take the outputs and output them... if it is div or mult we dont output anything but instead store values into HI or LO
  //   pretty sure this works cause div and mult are made to not change the Res in the main?
endmodule

module Control (
  input  [31:0] Inst,
  output [4:0] rs,
  output [4:0] rt,
  output [4:0] rd,
  output [31:0] imm,
  output reg_write_e,
  output imm_sel,
  output [3:0] ALU_code
);

  wire and_1_out, comparator_1_eq, comparator_2_gt, comparator_3_eq, comparator_4_eq, comparator_5_eq,
       comparator_6_eq, comparator_7_eq, comparator_8_eq, comparator_9_eq, comparator_10_eq,
       comparator_11_eq, comparator_12_eq, comparator_13_eq, not_1_out, or_1_out;
  wire [3:0] adder_1_out, adder_2_out, adder_3_out, adder_4_out, adder_5_out, adder_6_out, adder_7_out,
       adder_8_out, demultiplexer_1_out0, demultiplexer_1_out1, demultiplexer_2_out0, demultiplexer_2_out1,
       demultiplexer_3_out0, demultiplexer_3_out1, demultiplexer_4_out0, demultiplexer_4_out1,
       demultiplexer_5_out0, demultiplexer_5_out1, demultiplexer_6_out0, demultiplexer_6_out1,
       demultiplexer_7_out0, demultiplexer_7_out1, demultiplexer_8_out0, demultiplexer_8_out1,
       multiplexer_2_out, multiplexer_3_out, multiplexer_4_out, multiplexer_5_out, multiplexer_6_out,
       multiplexer_7_out, multiplexer_8_out, multiplexer_9_out, or_3_out;
  wire [15:0] multiplexer_10_out;

  Comparator #(.width(6)) comparator_1 (.a(Inst[31:26]), .b({6{1'b0}}), .eq(comparator_1_eq));  // open: gt, lt
  Comparator #(.width(5)) comparator_2 (.a(Inst[10:6]), .b({5{1'b0}}), .gt(comparator_2_gt));  // open: eq, lt
  not not_1 (not_1_out, comparator_1_eq);
  and and_1 (and_1_out, comparator_2_gt, comparator_1_eq);
  Comparator #(.width(6)) comparator_3 (.a(6'b100000), .b(Inst[5:0]), .eq(comparator_3_eq));  // open: gt, lt
  Comparator #(.width(6)) comparator_4 (.a(6'b100010), .b(Inst[5:0]), .eq(comparator_4_eq));  // open: gt, lt
  Comparator #(.width(6)) comparator_5 (.a(6'b011000), .b(Inst[5:0]), .eq(comparator_5_eq));  // open: gt, lt
  Comparator #(.width(6)) comparator_6 (.a(6'b011010), .b(Inst[5:0]), .eq(comparator_6_eq));  // open: gt, lt
  Comparator #(.width(6)) comparator_7 (.a(6'b010010), .b(Inst[5:0]), .eq(comparator_7_eq));  // open: gt, lt
  Comparator #(.width(6)) comparator_8 (.a(6'b010000), .b(Inst[5:0]), .eq(comparator_8_eq));  // open: gt, lt
  Comparator #(.width(6)) comparator_9 (.a({6{1'b0}}), .b(Inst[5:0]), .eq(comparator_9_eq));  // open: gt, lt
  Comparator #(.width(6)) comparator_10 (.a(6'b000010), .b(Inst[5:0]), .eq(comparator_10_eq));  // open: gt, lt
  Comparator #(.width(6)) comparator_11 (.a(6'b101010), .b(Inst[5:0]), .eq(comparator_11_eq));  // open: gt, lt
  Demultiplexer #(.width(4)) demultiplexer_1 (
    .out0(demultiplexer_1_out0), .out1(demultiplexer_1_out1), .in(4'b0000), .sel(comparator_3_eq));
  Demultiplexer #(.width(4)) demultiplexer_2 (
    .out0(demultiplexer_2_out0), .out1(demultiplexer_2_out1), .in(adder_1_out), .sel(comparator_4_eq));
  Demultiplexer #(.width(4)) demultiplexer_3 (
    .out0(demultiplexer_3_out0), .out1(demultiplexer_3_out1), .in(adder_2_out), .sel(comparator_5_eq));
  Demultiplexer #(.width(4)) demultiplexer_4 (
    .out0(demultiplexer_4_out0), .out1(demultiplexer_4_out1), .in(adder_3_out), .sel(comparator_6_eq));
  Demultiplexer #(.width(4)) demultiplexer_5 (
    .out0(demultiplexer_5_out0), .out1(demultiplexer_5_out1), .in(adder_4_out), .sel(comparator_7_eq));
  Demultiplexer #(.width(4)) demultiplexer_6 (
    .out0(demultiplexer_6_out0), .out1(demultiplexer_6_out1), .in(adder_5_out), .sel(comparator_8_eq));
  Demultiplexer #(.width(4)) demultiplexer_7 (
    .out0(demultiplexer_7_out0), .out1(demultiplexer_7_out1), .in(adder_6_out), .sel(comparator_9_eq));
  Demultiplexer #(.width(4)) demultiplexer_8 (
    .out0(demultiplexer_8_out0), .out1(demultiplexer_8_out1), .in(adder_7_out), .sel(comparator_10_eq));
  Adder #(.width(4)) adder_1 (.a(demultiplexer_1_out0), .b(4'b0001), .out(adder_1_out));  // open: cin, cout
  // Probe on adder_1_out
  Adder #(.width(4)) adder_2 (.a(demultiplexer_2_out0), .b(4'b0001), .out(adder_2_out));  // open: cin, cout
  // Probe on adder_2_out
  Adder #(.width(4)) adder_3 (.a(demultiplexer_3_out0), .b(4'b0001), .out(adder_3_out));  // open: cin, cout
  // Probe on adder_3_out
  Adder #(.width(4)) adder_4 (.a(demultiplexer_4_out0), .b(4'b0001), .out(adder_4_out));  // open: cin, cout
  // Probe on adder_4_out
  Adder #(.width(4)) adder_5 (.a(demultiplexer_5_out0), .b(4'b0001), .out(adder_5_out));  // open: cin, cout
  // Probe on adder_5_out
  Adder #(.width(4)) adder_6 (.a(demultiplexer_6_out0), .b(4'b0001), .out(adder_6_out));  // open: cin, cout
  // Probe on adder_6_out
  Adder #(.width(4)) adder_7 (.a(demultiplexer_7_out0), .b(4'b0001), .out(adder_7_out));  // open: cin, cout
  // Probe on adder_7_out
  Adder #(.width(4)) adder_8 (.a(demultiplexer_8_out0), .b(4'b0001), .out(adder_8_out));  // open: cin, cout
  // Probe on adder_8_out
  Multiplexer #(.width(5)) multiplexer_1 (.in0(Inst[25:21]), .in1(Inst[20:16]), .out(rs), .sel(and_1_out));
  or or_1 (or_1_out, not_1_out, and_1_out);
  Multiplexer #(.width(4)) multiplexer_2 (
    .in0(4'b0000), .in1(demultiplexer_2_out1), .out(multiplexer_2_out), .sel(comparator_4_eq));
  Multiplexer #(.width(4)) multiplexer_3 (
    .in0(4'b0000), .in1(demultiplexer_3_out1), .out(multiplexer_3_out), .sel(comparator_5_eq));
  Multiplexer #(.width(4)) multiplexer_4 (
    .in0(4'b0000), .in1(demultiplexer_4_out1), .out(multiplexer_4_out), .sel(comparator_6_eq));
  Multiplexer #(.width(4)) multiplexer_5 (
    .in0(4'b0000), .in1(demultiplexer_5_out1), .out(multiplexer_5_out), .sel(comparator_7_eq));
  Multiplexer #(.width(4)) multiplexer_6 (
    .in0(4'b0000), .in1(demultiplexer_6_out1), .out(multiplexer_6_out), .sel(comparator_8_eq));
  Multiplexer #(.width(4)) multiplexer_7 (
    .in0(4'b0000), .in1(demultiplexer_7_out1), .out(multiplexer_7_out), .sel(comparator_9_eq));
  Multiplexer #(.width(4)) multiplexer_8 (
    .in0(4'b0000), .in1(demultiplexer_8_out1), .out(multiplexer_8_out), .sel(comparator_10_eq));
  Multiplexer #(.width(4)) multiplexer_9 (
    .in0(4'b0000), .in1(adder_8_out), .out(multiplexer_9_out), .sel(comparator_11_eq));
  Multiplexer #(.width(16)) multiplexer_10 (
    .in0({16{1'b0}}), .in1(Inst[15:0]), .out(multiplexer_10_out), .sel(or_1_out));
  Comparator #(.width(4)) comparator_12 (.a(or_3_out), .b(4'b0010), .eq(comparator_12_eq));  // open: gt, lt
  Comparator #(.width(4)) comparator_13 (.a(or_3_out), .b(4'b0011), .eq(comparator_13_eq));  // open: gt, lt
  assign imm = {{16{multiplexer_10_out[15]}}, multiplexer_10_out};  // Bit_Extender bit_extender_1
  or or_2 (imm_sel, and_1_out, not_1_out);
  assign or_3_out = demultiplexer_1_out1 | multiplexer_2_out | multiplexer_3_out | multiplexer_4_out | multiplexer_5_out | multiplexer_6_out | multiplexer_7_out | multiplexer_8_out | multiplexer_9_out;  // OR_Gate or_3, 4 bits wide
  nor nor_1 (reg_write_e, comparator_12_eq, comparator_13_eq);
  Multiplexer #(.width(4)) multiplexer_11 (.in0(or_3_out), .in1(4'b0000), .out(ALU_code), .sel(not_1_out));

  assign rd = Inst[15:11];
  assign rt = Inst[20:16];

  // Notes on the sheet:
  //   R type
  //   not R type
  //   sll or srl
  //   USE THIS TO RETURN ONLY 32 BIT NUMBERS AND TO EXTEND IT
endmodule

module ignore (
  input  [31:0] in_1,
  input  [31:0] in_2
);

  wire and_1_out, and_2_out, and_3_out, and_4_out, clock_1_out, clock_2_out, control_1_imm_sel,
       control_2_imm_sel, control_3_imm_sel, control_4_imm_sel, multiplexer_1_out, multiplexer_5_out,
       not_1_out, not_2_out, or_1_out, or_2_out, regfile_1_p2, regfile_2_p2, regfile_3_p2, regfile_4_p2,
       undriven, undriven_4, undriven_5, undriven_6, undriven_7, undriven_8, undriven_9, undriven_10,
       undriven_13, undriven_14, undriven_15, undriven_16, undriven_17;
  wire [3:0] control_1_alu_code, control_2_alu_code, control_3_alu_code, control_4_alu_code;
  wire [4:0] regfile_1_p3, regfile_1_p4, regfile_1_p5, regfile_2_p3, regfile_2_p4, regfile_2_p5,
       regfile_3_p3, regfile_3_p4, regfile_3_p5, regfile_4_p3, regfile_4_p4, regfile_4_p5;
  wire [15:0] bit_extender_1_out, bit_extender_4_out;
  wire [25:0] bit_extender_2_out, bit_extender_5_out, shifter_3_out, shifter_6_out;
  wire [31:0] adder_1_out, adder_2_out, adder_3_out, adder_4_out, alu_1_res, alu_3_res, alu_4_res,
       control_1_imm, control_3_imm, multiplexer_2_out, multiplexer_3_out, multiplexer_4_out,
       multiplexer_6_out, multiplexer_7_out, multiplexer_8_out, multiplexer_9_out, multiplexer_10_out,
       multiplexer_11_out, regfile_1_p6, regfile_1_p7, regfile_2_p1, regfile_2_p6, regfile_2_p7,
       regfile_3_p6, regfile_3_p7, regfile_4_p6, regfile_4_p7, register_1_q, register_2_q, rom_1_data,
       rom_2_data, shifter_1_out, shifter_2_out, shifter_4_out, shifter_5_out, undriven_2, undriven_3,
       undriven_11, undriven_12;

  Multiplexer multiplexer_1 (.in0(alu_1_res[0]), .in1(undriven), .out(multiplexer_1_out), .sel(undriven_4));
  // regfile regfile_1: pin names not known; wires that end beside it: multiplexer_1_out, regfile_1_p2, regfile_1_p3, regfile_1_p4, regfile_1_p5, regfile_1_p6, regfile_1_p7
  Adder #(.width(32)) adder_1 (.a(register_1_q), .b(32'h4), .out(adder_1_out));  // open: cin, cout
  Clock clock_1 (.out(clock_1_out));
  Adder #(.width(32)) adder_2 (.a(adder_1_out), .b(undriven_2), .out(adder_2_out));  // open: cin, cout
  Shifter #(.width(32)) shifter_1 (.in(undriven_2), .\dist (5'b00010), .out(shifter_1_out));
  Register #(.width(32)) register_1 (
    .D(multiplexer_3_out), .en(1'b1), .clk(clock_1_out), .Q(register_1_q));  // open: clr
  Multiplexer #(.width(32)) multiplexer_2 (
    .in0(adder_1_out), .in1(adder_2_out), .out(multiplexer_2_out), .sel(or_1_out));
  Control control_1 (
    .Inst(in_1), .rs(regfile_1_p4), .rt(regfile_1_p5), .rd(regfile_1_p3), .imm(control_1_imm),
    .reg_write_e(regfile_1_p2), .imm_sel(control_1_imm_sel), .ALU_code(control_1_alu_code));
  Shifter #(.shift("lr"), .width(32)) shifter_2 (.in(register_1_q), .\dist (5'b00010), .out(shifter_2_out));
  Multiplexer #(.width(32)) multiplexer_3 (
    .in0(multiplexer_2_out), .in1(undriven_3), .out(multiplexer_3_out), .sel(undriven_5));
  Multiplexer #(.width(32)) multiplexer_4 (
    .in0(regfile_1_p7), .in1(control_1_imm), .out(multiplexer_4_out), .sel(control_1_imm_sel));
  ROM #(.addrWidth(16), .dataWidth(32)) rom_1 (.addr(bit_extender_1_out), .data(rom_1_data));
  Bit_Extender #(.in_width(32)) bit_extender_1 (.in(shifter_2_out), .out(bit_extender_1_out));
  Bit_Extender #(.in_width(32), .out_width(26)) bit_extender_2 (.in(undriven_3), .out(bit_extender_2_out));
  or or_1 (or_1_out, and_2_out, and_1_out);
  Shifter #(.width(26)) shifter_3 (.in(bit_extender_2_out), .\dist (5'b00010), .out(shifter_3_out));
  ALU alu_1 (.OP2(multiplexer_4_out), .OP1(regfile_1_p6), .ALU_CODE(control_1_alu_code), .Res(alu_1_res));
  and and_1 (and_1_out, undriven_8, undriven_6);
  assign rom_1_data = {{6{shifter_3_out[25]}}, shifter_3_out};  // Bit_Extender bit_extender_3
  and and_2 (and_2_out, not_1_out, undriven_7);
  not not_1 (not_1_out, undriven_8);
  Multiplexer multiplexer_5 (.in0(alu_3_res[0]), .in1(undriven_10), .out(multiplexer_5_out), .sel(undriven_9));
  // regfile regfile_2: pin names not known; wires that end beside it: regfile_2_p1, regfile_2_p2, regfile_2_p3, regfile_2_p4, regfile_2_p5, regfile_2_p6, regfile_2_p7
  Control control_2 (
    .Inst(rom_1_data), .rs(regfile_2_p4), .rt(regfile_2_p5), .rd(regfile_2_p3), .imm(shifter_1_out),
    .reg_write_e(regfile_2_p2), .imm_sel(control_2_imm_sel), .ALU_code(control_2_alu_code));
  // regfile regfile_3: pin names not known; wires that end beside it: multiplexer_5_out, regfile_3_p2, regfile_3_p3, regfile_3_p4, regfile_3_p5, regfile_3_p6, regfile_3_p7
  Multiplexer #(.width(32)) multiplexer_6 (
    .in0(regfile_2_p7), .in1(shifter_1_out), .out(multiplexer_6_out), .sel(control_2_imm_sel));
  Control control_3 (
    .Inst(in_2), .rs(regfile_3_p4), .rt(regfile_3_p5), .rd(regfile_3_p3), .imm(control_3_imm),
    .reg_write_e(regfile_3_p2), .imm_sel(control_3_imm_sel), .ALU_code(control_3_alu_code));
  ALU alu_2 (.OP2(multiplexer_6_out), .OP1(regfile_2_p6), .ALU_CODE(control_2_alu_code), .Res(regfile_2_p1));
  Multiplexer #(.width(32)) multiplexer_7 (
    .in0(regfile_3_p7), .in1(control_3_imm), .out(multiplexer_7_out), .sel(control_3_imm_sel));
  ALU alu_3 (.OP2(multiplexer_7_out), .OP1(regfile_3_p6), .ALU_CODE(control_3_alu_code), .Res(alu_3_res));
  Adder #(.width(32)) adder_3 (.a(adder_4_out), .b(undriven_11), .out(adder_3_out));  // open: cin, cout
  Adder #(.width(32)) adder_4 (.a(register_2_q), .b(32'h4), .out(adder_4_out));  // open: cin, cout
  Clock clock_2 (.out(clock_2_out));
  Shifter #(.width(32)) shifter_4 (.in(undriven_11), .\dist (5'b00010), .out(shifter_4_out));
  Register #(.width(32)) register_2 (
    .D(multiplexer_9_out), .en(1'b1), .clk(clock_2_out), .Q(register_2_q));  // open: clr
  Multiplexer #(.width(32)) multiplexer_8 (
    .in0(adder_4_out), .in1(adder_3_out), .out(multiplexer_8_out), .sel(or_2_out));
  Shifter #(.shift("lr"), .width(32)) shifter_5 (.in(register_2_q), .\dist (5'b00010), .out(shifter_5_out));
  Multiplexer #(.width(32)) multiplexer_9 (
    .in0(multiplexer_8_out), .in1(undriven_12), .out(multiplexer_9_out), .sel(undriven_13));
  ROM #(.addrWidth(16), .dataWidth(32)) rom_2 (.addr(bit_extender_4_out), .data(rom_2_data));
  Bit_Extender #(.in_width(32)) bit_extender_4 (.in(shifter_5_out), .out(bit_extender_4_out));
  Bit_Extender #(.in_width(32), .out_width(26)) bit_extender_5 (.in(undriven_12), .out(bit_extender_5_out));
  or or_2 (or_2_out, and_3_out, and_4_out);
  Shifter #(.width(26)) shifter_6 (.in(bit_extender_5_out), .\dist (5'b00010), .out(shifter_6_out));
  and and_3 (and_3_out, not_2_out, undriven_15);
  and and_4 (and_4_out, undriven_17, undriven_14);
  assign rom_2_data = {{6{shifter_6_out[25]}}, shifter_6_out};  // Bit_Extender bit_extender_6
  not not_2 (not_2_out, undriven_17);
  Multiplexer #(.width(32)) multiplexer_10 (
    .in0(adder_4_out), .in1(alu_4_res), .out(multiplexer_10_out), .sel(undriven_16));
  // regfile regfile_4: pin names not known; wires that end beside it: multiplexer_10_out, regfile_4_p2, regfile_4_p3, regfile_4_p4, regfile_4_p5, regfile_4_p6, regfile_4_p7
  Control control_4 (
    .Inst(rom_2_data), .rs(regfile_4_p4), .rt(regfile_4_p5), .rd(regfile_4_p3), .imm(shifter_4_out),
    .reg_write_e(regfile_4_p2), .imm_sel(control_4_imm_sel), .ALU_code(control_4_alu_code));
  Multiplexer #(.width(32)) multiplexer_11 (
    .in0(regfile_4_p7), .in1(shifter_4_out), .out(multiplexer_11_out), .sel(control_4_imm_sel));
  ALU alu_4 (.OP2(multiplexer_11_out), .OP1(regfile_4_p6), .ALU_CODE(control_4_alu_code), .Res(alu_4_res));
  // Pins of 1 and 32 bits meet at alu_3_res
  // Pins of 1 and 32 bits meet at alu_1_res

  // Notes on the sheet:
  //   lw $t0, 4($t1)
  //   beq and bne AND SOME J
  //   should branch
  //   new control outputs
  //   HALFWAY THROUGH JUMP GOT CONFUSED -- SEE PIC ON THE PHONE - MIGHT WORK MIGHT NOT
  //   NEED TO FIGURE OUT IF WE WANT SIGNED OR UNSIGNED EXTENDERS.... FOR TRIMMING BITS IT DOESNT MATTER
  //   think it works but lowkey got lost so we will need to check
  //   need it to work for beq
  //   immediate
  //   they had a extender cause immedicate might end up being less than 32 bits
  //   new output
  //   t1
  //   read ram
  //   4
  //   we need the immediate to be the offset for ram
  //   add
  //   WANT SIGNED IDK WHICH ONE THIS IS
  //   add ram reading functionality
  //   new ALU codes
  //   false
  //   ram write enable
  //   ram output
  //   ram read in as well as shifter and bit extender (making it word readable)
  //   SHOULD AT LEAST WORK FOR ADD, ADDI AND MULT
  //   is beq
  //   IS J
  //   is bne
  //   SET THIS TO 0 IF YOU DO NOT WANT TO OVERWRITE REGISTERS ... EX MULT -- HI AND LOW LIVE  IN THE ALU
  //   FOR MULT YOU DON'T WANT TO CHANGE ANY REGISTERS
  //   sw $t0, 4($t1)
  //   MULITPLEXER USED TO DETERMINE WHETHER IT IS I TYPE OR R TYPE
  //   BASICALLLY MAKE THIS = TO ZERO TO TAKE THE R TYPE 
  //   new control outputs
  //   new output
  //   t1
  //   t0
  //   read ram
  //   eq
  //   4
  //   we need the immediate to be the offset for ram
  //   add
  //   new ALU codes
  //   new output shows what this is a beq/bne and the imputs are the same
  //   add ram reading functionality
  //   true
  //   ram write enable
  //   ram output
  //   ram read in as well as shifter and bit extender (making it word readable)
  //   ram input register part
  //   FOR JAL
  //   ADDING JAL
  //   should branch
  //   need it to work for beq
  //   immediate
  //   they had a extender cause immedicate might end up being less than 32 bits
  //   WANT SIGNED IDK WHICH ONE THIS IS
  //   FOR JAL
  //   SHOULD AT LEAST WORK FOR ADD, ADDI AND MULT
  //   IS J
  //   IS JAL
  //   is beq
  //   SET THIS TO 0 IF YOU DO NOT WANT TO OVERWRITE REGISTERS ... EX MULT -- HI AND LOW LIVE  IN THE ALU
  //   is bne
  //   FOR MULT YOU DON'T WANT TO CHANGE ANY REGISTERS
  //   MULITPLEXER USED TO DETERMINE WHETHER IT IS I TYPE OR R TYPE
  //   BASICALLLY MAKE THIS = TO ZERO TO TAKE THE R TYPE 
  //   eq
  //   new output shows what this is a beq/bne and the imputs are the same
endmodule
