// Logisim project Proj2starter.circ as structural Verilog: 4 circuits, main circuit regfile
module CPUmain (
  input  [31:0] in_1
);

  wire control_1_imm_sel, control_1_reg_write_e;
  wire [3:0] control_1_alu_code;
  wire [4:0] control_1_rd, control_1_rs, control_1_rt;
  wire [31:0] alu_1_res, control_1_imm, multiplexer_1_out, regfile_1_rs_data, regfile_1_rt_data;

  regfile regfile_1 (
    .rt(control_1_rt), .rd(control_1_rd), .rd_data(alu_1_res), .write_e(control_1_reg_write_e),
    .rs(control_1_rs), .rs_data(regfile_1_rs_data), .rt_data(regfile_1_rt_data));
  Control control_1 (
    .Inst(in_1), .rs(control_1_rs), .rt(control_1_rt), .rd(control_1_rd), .imm(control_1_imm),
    .reg_write_e(control_1_reg_write_e), .imm_sel(control_1_imm_sel), .ALU_code(control_1_alu_code));
  Multiplexer #(.width(32)) multiplexer_1 (
    .in0(regfile_1_rt_data), .in1(control_1_imm), .out(multiplexer_1_out), .sel(control_1_imm_sel));
  Bit_Extender bit_extender_1 ();  // open: in, out
  ALU alu_1 (.OP2(multiplexer_1_out), .OP1(regfile_1_rs_data), .ALU_CODE(control_1_alu_code), .Res(alu_1_res));

  // Notes on the sheet:
  //   SHOULD AT LEAST WORK FOR ADD, ADDI AND MULT
  //   SET THIS TO 0 IF YOU DO NOT WANT TO OVERWRITE REGISTERS ... EX MULT -- HI AND LOW LIVE  IN THE ALU
  //   FOR MULT YOU DON'T WANT TO CHANGE ANY REGISTERS
  //   MULITPLEXER USED TO DETERMINE WHETHER IT IS I TYPE OR R TYPE
  //   BASICALLLY MAKE THIS = TO ZERO TO TAKE THE R TYPE 
  //   USE THIS TO EXTEND NON 32 BIT NUMBERS INTO SIGNED 32 BIT NUMBERS
  //   ALU DOES ALL OPERATIONS ON EVERY OP1 AND OP2 FROM THE REGISTERS -- HOWEVER YOU NEED TO SPECIFY WHICH ONE TO GET FROM THE ALU CODE
endmodule

module regfile (
  input  [4:0] rs,
  input  [4:0] rt,
  input  [4:0] rd,
  input  write_e,
  input  [31:0] rd_data,
  output [31:0] rs_data,
  output [31:0] rt_data
);

  Register Reg1_at ();  // open: D, en, clk, Q, clr
endmodule

module ALU (
  input  [3:0] ALU_CODE,
  input  [31:0] OP1,
  input  [31:0] OP2,
  output [31:0] Res
);

  Adder #(.width(32)) adder_1 (.a(OP1), .b(OP2));  // open: out, cin, cout
  Subtractor #(.width(32)) subtractor_1 (.a(OP1), .b(OP2));  // open: out, bin, bout
  Multiplier #(.width(32)) multiplier_1 (.a(OP1), .b(OP2));  // open: out, cin, cout
  Divider #(.width(32)) divider_1 (.a(OP1), .b(OP2));  // open: out, upper, rem
  Register HI ();  // open: D, en, clk, Q, clr
  Register LO ();  // open: D, en, clk, Q, clr
endmodule

module Control (
  input  [31:0] Inst,
  output [4:0] rs,
  output [4:0] rt,
  output [4:0] rd,
  output [31:0] imm,
  output reg_write_e,
  output imm_sel,
  output [3:0] ALU_code
);

  Bit_Extender bit_extender_1 ();  // open: in, out

  // Notes on the sheet:
  //   USE THIS TO RETURN ONLY 32 BIT NUMBERS AND TO EXTEND IT
endmodule
